# Fritzing sketch diagram (saved by Fritzing 0.9.3b)
breadboards: 1

parts:
  Part1 = Photon
  Part2 = Adafruit BME680

nets:
  GND: Part1.GND, Part2.GND
  N1: Part1.D0, Part2.SDI/SDA
  N2: Part1.D1, Part2.SCK/SCL
  3V3: Part1.3V3, Part2.VIN
