# Fritzing sketch button (saved by Fritzing 0.9.3b)
breadboards: 1

parts:
  Part1 = Photon
  BUTTON1 = Arcade Button (red)
  LED1 = LED - 5mm [color="Red (633nm)" package="5 mm [THT]"]

nets:
  N1: Part1.GND, LED1.cathode
  N2: Part1.VIN, LED1.anode
  N3: Part1.D5, BUTTON1.no_name_yet#2
  N4: Part1.3V3, BUTTON1.no_name_yet#1

notes:
  Technically, the LED is embedded in the arcade button. It has 2 LEDs in parallel with 1k resistors each.
  Requires 5V with 10mA draw

custom parts:
  Arcade Button (red): Adafruit Arcade Button (red)
