# Fritzing sketch diagram (saved by Fritzing 0.9.3b)
breadboards: 1

parts:
  Part1 = Photon
  Part2 = Adafruit BME680
  R1 = Resistor [tolerance=±5% resistance=220 package=THT]
  LED1 = LED - 5mm [color="Red (633nm)" package="5 mm [THT]"]

nets:
  GND: Part1.GND, Part2.GND, R1.Pin_0
  N1: Part1.D0, Part2.SDI/SDA
  N2: Part1.D1, Part2.SCK/SCL
  N3: Part1.D4, LED1.anode
  3V3: Part1.3V3, Part2.VIN
  N4: R1.Pin_1, LED1.cathode
